// Logisim project ISA.circ as structural Verilog: 5 circuits, main circuit my circuit
module my_circuit (
  input  in_1,
  input  in_2,
  input  in_3,
  input  in_4,
  input  in_5,
  input  in_6,
  input  in_7,
  input  in_8,
  input  in_9,
  input  in_10
);

  wire [5:0] OPCODE;
  wire [17:0] IMM;
  wire [25:18] IR_q;
  wire [31:0] adder_1_out, alu_1_output, bit_extender_1_out, memory_1_mdr_out, multiplexer_1_out, PC_q,
       register_file_1_out_a, register_file_1_out_b;

  Adder #(.width(32)) adder_1 (.a(PC_q), .b(32'h4), .out(adder_1_out));  // open: cin, cout
  Register #(.width(32)) PC (.D(adder_1_out), .en(in_2), .Q(PC_q), .clk(in_3), .clr(in_4));
  Register #(.width(32)) IR (.D(alu_1_output), .en(in_7), .Q({OPCODE, IR_q, IMM}), .clk(in_3));  // open: clr
  register_file register_file_1 (
    .REG_A(IR_q[21:18]), .REG_B(IMM[3:0]), .DST_REG(IR_q[25:22]), .DATA_IN(alu_1_output), .WE(in_10),
    .CK(in_3), .OUT_A(register_file_1_out_a), .OUT_B(register_file_1_out_b));
  Multiplexer #(.width(32), .disabled(0), .enable("false")) multiplexer_1 (
    .in0(register_file_1_out_b), .in1(bit_extender_1_out), .out(multiplexer_1_out), .sel(OPCODE[4]));
  assign bit_extender_1_out = {{14{1'b0}}, IMM};  // Bit_Extender bit_extender_1
  ALU alu_1 (.INPUT_A(register_file_1_out_a), .INPUT_B(multiplexer_1_out), .SELECT(OPCODE[2:0]), .OUTPUT(alu_1_output));
  memory memory_1 (
    .MAR_IN(PC_q), .CK(in_3), .LOAD(in_9), .SIZE(in_8), .LD_MAR(in_5), .LD_MDR(in_6),
    .MDR_OUT(memory_1_mdr_out));  // open: MDR_IN
  assign alu_1_output = in_1 ? memory_1_mdr_out : 32'bz;  // Controlled_Buffer controlled_buffer_1

  // Other names for the same wires on the sheet: BYTE = in_8; CK = in_3; CLR_PC = in_4; LD_IR = in_7; LD_MAR = in_5;
  //   LD_MDR = in_6; LD_MEM = in_9; LD_PC = in_2; LD_RG = in_10
endmodule

module memory (
  input  [31:0] MDR_IN,
  input  [31:0] MAR_IN,
  input  LD_MAR,
  input  LD_MDR,
  input  CK,
  input  LOAD,
  input  SIZE,
  output [31:0] MDR_OUT
);

  wire not_1_out;
  wire [1:0] BYTE;
  wire [5:0] CRAP;
  wire [7:0] multiplexer_1_out, ram_1_data, ram_2_data, ram_3_data, ram_4_data;
  wire [25:2] MAR_q;
  wire [31:0] bit_extender_1_out, demultiplexer_1_out0, MDR_IN_t, multiplexer_2_out;

  Register #(.width(32)) MAR (.D(MAR_IN), .en(LD_MAR), .Q({CRAP, MAR_q, BYTE}), .clk(CK));  // open: clr
  RAM #(.addrWidth(24)) ram_1 (.addr(MAR_q), .data(ram_1_data), .clk(CK), .ld(LOAD));  // open: sel, clr
  RAM #(.addrWidth(24)) ram_2 (.addr(MAR_q), .data(ram_2_data), .clk(CK), .ld(LOAD));  // open: sel, clr
  RAM #(.addrWidth(24)) ram_3 (.addr(MAR_q), .data(ram_3_data), .clk(CK), .ld(LOAD));  // open: sel, clr
  RAM #(.addrWidth(24)) ram_4 (.addr(MAR_q), .data(ram_4_data), .clk(CK), .ld(LOAD));  // open: sel, clr
  not not_1 (not_1_out, LOAD);
  Multiplexer #(.select(2), .width(8), .disabled(0), .enable("false")) multiplexer_1 (
    .in0(ram_1_data), .in1(ram_2_data), .in2(ram_3_data), .in3(ram_4_data), .out(multiplexer_1_out),
    .sel(BYTE));
  Demultiplexer #(.width(32), .disabled(0), .enable("false")) demultiplexer_1 (
    .out0(demultiplexer_1_out0), .out1(MDR_IN_t), .in(MDR_IN), .sel(SIZE));
  assign {ram_4_data, ram_3_data, ram_2_data, ram_1_data} = not_1_out ? demultiplexer_1_out0 : 32'bz;  // Controlled_Buffer controlled_buffer_1
  assign bit_extender_1_out = {{24{1'b0}}, multiplexer_1_out};  // Bit_Extender bit_extender_1
  Multiplexer #(.width(32), .disabled(0), .enable("false")) multiplexer_2 (
    .in0({ram_4_data, ram_3_data, ram_2_data, ram_1_data}), .in1(bit_extender_1_out),
    .out(multiplexer_2_out), .sel(SIZE));
  Register #(.width(32)) MDR (.D(multiplexer_2_out), .en(LD_MDR), .Q(MDR_OUT), .clk(CK));  // open: clr

  // Other names for the same wires on the sheet: L = LOAD
endmodule

module register_file (
  input  [3:0] DST_REG,
  input  [31:0] DATA_IN,
  input  [3:0] REG_A,
  input  [3:0] REG_B,
  input  CK,
  input  WE,
  output [31:0] OUT_A,
  output [31:0] OUT_B
);

  wire demultiplexer_1_out0, demultiplexer_1_out1, demultiplexer_1_out2, demultiplexer_1_out3;
  wire [31:0] register_group_1_out_a, register_group_1_out_b, register_group_2_out_a, register_group_2_out_b,
       register_group_3_out_a, register_group_3_out_b, register_group_4_out_a, register_group_4_out_b;

  Demultiplexer #(.select(2), .disabled(0), .enable("false")) demultiplexer_1 (
    .out0(demultiplexer_1_out0), .out1(demultiplexer_1_out1), .out2(demultiplexer_1_out2),
    .out3(demultiplexer_1_out3), .in(WE), .sel(DST_REG[3:2]));
  register_group register_group_1 (
    .REG_A(REG_A[1:0]), .REG_B(REG_B[1:0]), .DATA_IN(DATA_IN), .DST_REG(DST_REG[1:0]),
    .WE(demultiplexer_1_out0), .CK(CK), .OUT_A(register_group_1_out_a), .OUT_B(register_group_1_out_b));
  register_group register_group_2 (
    .REG_A(REG_A[1:0]), .REG_B(REG_B[1:0]), .DATA_IN(DATA_IN), .DST_REG(DST_REG[1:0]),
    .WE(demultiplexer_1_out1), .CK(CK), .OUT_A(register_group_2_out_a), .OUT_B(register_group_2_out_b));
  register_group register_group_3 (
    .REG_A(REG_A[1:0]), .REG_B(REG_B[1:0]), .DATA_IN(DATA_IN), .DST_REG(DST_REG[1:0]),
    .WE(demultiplexer_1_out2), .CK(CK), .OUT_A(register_group_3_out_a), .OUT_B(register_group_3_out_b));
  register_group register_group_4 (
    .REG_A(REG_A[1:0]), .REG_B(REG_B[1:0]), .DATA_IN(DATA_IN), .DST_REG(DST_REG[1:0]),
    .WE(demultiplexer_1_out3), .CK(CK), .OUT_A(register_group_4_out_a), .OUT_B(register_group_4_out_b));
  Multiplexer #(.select(2), .width(32), .disabled(0), .enable("false")) multiplexer_1 (
    .in0(register_group_1_out_a), .in1(register_group_2_out_a), .in2(register_group_3_out_a),
    .in3(register_group_4_out_a), .out(OUT_A), .sel(REG_A[3:2]));
  Multiplexer #(.select(2), .width(32), .disabled(0), .enable("false")) multiplexer_2 (
    .in0(register_group_1_out_b), .in1(register_group_2_out_b), .in2(register_group_3_out_b),
    .in3(register_group_4_out_b), .out(OUT_B), .sel(REG_B[3:2]));

  // Other names for the same wires on the sheet: D_REG[1:0] = DST_REG[1:0]; D_GRP[1:0] = DST_REG[3:2];
  //   A_REG[1:0] = REG_A[1:0]; A_GRP[1:0] = REG_A[3:2]; B_REG[1:0] = REG_B[1:0]; B_GRP[1:0] = REG_B[3:2]
endmodule

module register_group (
  input  [31:0] DATA_IN,
  input  [1:0] DST_REG,
  input  [1:0] REG_A,
  input  [1:0] REG_B,
  input  WE,
  input  CK,
  output [31:0] OUT_A,
  output [31:0] OUT_B
);

  wire demultiplexer_1_out0, demultiplexer_1_out1, demultiplexer_1_out2, demultiplexer_1_out3;
  wire [31:0] register_1_q, register_2_q, register_3_q, register_4_q;

  Demultiplexer #(.select(2), .disabled(0), .enable("false")) demultiplexer_1 (
    .out0(demultiplexer_1_out0), .out1(demultiplexer_1_out1), .out2(demultiplexer_1_out2),
    .out3(demultiplexer_1_out3), .in(WE), .sel(DST_REG));
  Register #(.width(32)) register_1 (.D(DATA_IN), .en(demultiplexer_1_out0), .Q(register_1_q), .clk(CK));  // open: clr
  Register #(.width(32)) register_2 (.D(DATA_IN), .en(demultiplexer_1_out1), .Q(register_2_q), .clk(CK));  // open: clr
  Register #(.width(32)) register_3 (.D(DATA_IN), .en(demultiplexer_1_out2), .Q(register_3_q), .clk(CK));  // open: clr
  Register #(.width(32)) register_4 (.D(DATA_IN), .en(demultiplexer_1_out3), .Q(register_4_q), .clk(CK));  // open: clr
  Multiplexer #(.select(2), .width(32), .disabled(0), .enable("false")) multiplexer_1 (
    .in0(register_1_q), .in1(register_2_q), .in2(register_3_q), .in3(register_4_q), .out(OUT_A), .sel(REG_A));
  Multiplexer #(.select(2), .width(32), .disabled(0), .enable("false")) multiplexer_2 (
    .in0(register_1_q), .in1(register_2_q), .in2(register_3_q), .in3(register_4_q), .out(OUT_B), .sel(REG_B));
endmodule

module ALU (
  input  [2:0] SELECT,
  input  [31:0] INPUT_A,
  input  [31:0] INPUT_B,
  output [31:0] OUTPUT
);

  wire [31:0] adder_1_out, and_1_out, not_1_out;

  Adder #(.width(32)) adder_1 (.a(INPUT_A), .b(INPUT_B), .out(adder_1_out));  // open: cin, cout
  assign and_1_out = INPUT_A & INPUT_B;  // AND_Gate and_1, 32 bits wide
  assign not_1_out = ~and_1_out;  // NOT_Gate not_1, 32 bits wide
  Multiplexer #(.select(3), .width(32), .disabled(0), .enable("false")) multiplexer_1 (
    .in0(adder_1_out), .in1(not_1_out), .out(OUTPUT), .sel(SELECT));  // open: in2, in3, in4, in5, in6, in7

  // Other names for the same wires on the sheet: IN_A[31:0] = INPUT_A; IN_B[31:0] = INPUT_B
endmodule
