// Logisim project ISA-Interrupts.circ as structural Verilog: 8 circuits, main circuit my circuit
module my_circuit (
  input  in_1
);

  wire ADD_IMM, BYTE, DrALU, DrALU2, DrMEM, DrPC, DrPC2, DrREG, IE, JUMP, LD_IE, LD_IR, LD_MAR, LD_MDR,
       LD_PC, LD_RG, LD_Z, nor_1_out, or_1_out, Unaligned, Z;
  wire [1:0] Int;
  wire [2:0] ALU;
  wire [3:0] multiplexer_2_out, multiplexer_3_out;
  wire [4:1] Misc;
  wire [5:0] OPCODE;
  wire [15:0] controlled_buffer_2_out, controlled_buffer_2_out_2;
  wire [17:0] IMM;
  wire [25:18] IR_q;
  wire [31:0] adder_1_out, alu_1_output, bit_extender_1_out, controlled_buffer_1_out, memory_1_mdr_out,
       multiplexer_1_out, multiplexer_4_out, multiplexer_5_out, PC, register_file_1_out_a,
       register_file_1_out_b;

  Adder #(.width(32)) adder_1 (.a(PC), .b(32'h4), .out(adder_1_out));  // open: cin, cout
  Multiplexer #(.width(32), .disabled(0), .enable("false")) multiplexer_1 (
    .in0(adder_1_out), .in1({controlled_buffer_2_out_2, controlled_buffer_2_out}), .out(multiplexer_1_out),
    .sel(JUMP));
  Control_Unit control_unit_1 (
    .Z(Z), .OPCODE(OPCODE), .Interrupt(Int), .CK(in_1),
    .DATA_PATH({DrPC, DrPC2, DrALU, DrALU2, DrREG, DrMEM, LD_PC, LD_MAR, LD_MDR, LD_IR, LD_RG, LD_Z, Misc[4], BYTE, ADD_IMM, Misc[1], JUMP, ALU}));
  assign controlled_buffer_1_out = DrPC ? PC : 32'bz;  // Controlled_Buffer controlled_buffer_1
  Register #(.width(32)) u_PC (.D(multiplexer_1_out), .en(LD_PC), .Q(PC), .clk(in_1));  // open: clr
  assign {controlled_buffer_2_out_2, controlled_buffer_2_out} = DrPC2 ? PC : 32'bz;  // Controlled_Buffer controlled_buffer_2
  Register #(.width(32)) IR (
    .D({controlled_buffer_2_out_2, controlled_buffer_2_out}), .en(LD_IR), .Q({OPCODE, IR_q, IMM}), .clk(in_1));  // open: clr
  or or_1 (or_1_out, Misc[4], JUMP);
  Multiplexer #(.width(4), .disabled(0), .enable("false")) multiplexer_2 (
    .in0(IR_q[25:22]), .in1(IR_q[21:18]), .out(multiplexer_2_out), .sel(JUMP));
  register_file register_file_1 (
    .REG_A(IR_q[21:18]), .REG_B(multiplexer_3_out), .DST_REG(multiplexer_2_out),
    .DATA_IN({controlled_buffer_2_out_2, controlled_buffer_2_out}), .WE(LD_RG), .CK(in_1),
    .OUT_A(register_file_1_out_a), .OUT_B(register_file_1_out_b));
  Multiplexer #(.width(4), .disabled(0), .enable("false")) multiplexer_3 (
    .in0(IMM[3:0]), .in1(IR_q[25:22]), .out(multiplexer_3_out), .sel(or_1_out));
  nor nor_1 (nor_1_out, controlled_buffer_2_out_2[15], controlled_buffer_2_out_2[14], controlled_buffer_2_out_2[13], controlled_buffer_2_out_2[12], controlled_buffer_2_out_2[11], controlled_buffer_2_out_2[10], controlled_buffer_2_out_2[9], controlled_buffer_2_out_2[8], controlled_buffer_2_out_2[7], controlled_buffer_2_out_2[6], controlled_buffer_2_out_2[5], controlled_buffer_2_out_2[4], controlled_buffer_2_out_2[3], controlled_buffer_2_out_2[2], controlled_buffer_2_out_2[1], controlled_buffer_2_out_2[0], controlled_buffer_2_out[15], controlled_buffer_2_out[14], controlled_buffer_2_out[13], controlled_buffer_2_out[12], controlled_buffer_2_out[11], controlled_buffer_2_out[10], controlled_buffer_2_out[9], controlled_buffer_2_out[8], controlled_buffer_2_out[7], controlled_buffer_2_out[6], controlled_buffer_2_out[5], controlled_buffer_2_out[4], controlled_buffer_2_out[3], controlled_buffer_2_out[2], controlled_buffer_2_out[1], controlled_buffer_2_out[0]);
  Register #(.width(1)) u_Z (.D(nor_1_out), .en(LD_Z), .Q(Z), .clk(in_1));  // open: clr
  assign {controlled_buffer_2_out_2, controlled_buffer_2_out} = DrREG ? register_file_1_out_b : 32'bz;  // Controlled_Buffer controlled_buffer_3
  Multiplexer #(.width(32), .disabled(0), .enable("false")) multiplexer_4 (
    .in0(register_file_1_out_a), .in1(PC), .out(multiplexer_4_out), .sel(Misc[1]));
  Multiplexer #(.width(32), .disabled(0), .enable("false")) multiplexer_5 (
    .in0(register_file_1_out_b), .in1(bit_extender_1_out), .out(multiplexer_5_out), .sel(ADD_IMM));
  assign bit_extender_1_out = {{14{IMM[17]}}, IMM};  // Bit_Extender bit_extender_1
  assign controlled_buffer_1_out = DrALU ? alu_1_output : 32'bz;  // Controlled_Buffer controlled_buffer_4
  ALU alu_1 (.INPUT_A(multiplexer_4_out), .INPUT_B(multiplexer_5_out), .SELECT(ALU), .OUTPUT(alu_1_output));
  assign {controlled_buffer_2_out_2, controlled_buffer_2_out} = DrALU2 ? alu_1_output : 32'bz;  // Controlled_Buffer controlled_buffer_5
  Register #(.width(1)) u_IE (.en(LD_IE), .Q(IE), .clk(in_1));  // open: D, clr
  interrupt_control interrupt_control_1 ();  // open: in_1, Unaligned, IntACK, Clock, BUS, Int
  memory memory_1 (
    .MAR_IN(controlled_buffer_1_out), .Unaligned(Unaligned),
    .MDR_IN({controlled_buffer_2_out_2, controlled_buffer_2_out}), .CK(in_1), .STORE(Misc[4]), .SIZE(BYTE),
    .LD_MAR(LD_MAR), .LD_MDR(LD_MDR), .MDR_OUT(memory_1_mdr_out));
  assign {controlled_buffer_2_out_2, controlled_buffer_2_out} = DrMEM ? memory_1_mdr_out : 32'bz;  // Controlled_Buffer controlled_buffer_6

  // Other names for the same wires on the sheet: Misc (some bits) = {BYTE, ADD_IMM, JUMP}; PCOFF = Misc[1];
  //   STORE = Misc[4]; LOAD[5:0] = {LD_PC, LD_MAR, LD_MDR, LD_IR, LD_RG, LD_Z};
  //   DRs[5:0] = {DrPC, DrPC2, DrALU, DrALU2, DrREG, DrMEM}; CK = in_1

  // Notes on the sheet:
  //   CLOCK
  //   Eric Peyton
  //   GTID: 902705905
endmodule

module memory (
  input  [31:0] MDR_IN,
  input  [31:0] MAR_IN,
  input  LD_MAR,
  input  LD_MDR,
  input  CK,
  input  STORE,
  input  SIZE,
  output Unaligned,
  output [31:0] MDR_OUT
);

  wire and_3_out, demultiplexer_1_out0, demultiplexer_1_out1, demultiplexer_1_out2, demultiplexer_1_out3, L,
       not_2_out, not_3_out, not_4_out, not_5_out, not_6_out, or_1_out, or_2_out, or_3_out, or_4_out,
       or_5_out, SW;
  wire [1:0] BYTE;
  wire [5:0] CRAP;
  wire [7:0] MDR_IN_t, multiplexer_1_out, ram_1_data, ram_2_data, ram_3_data, ram_4_data;
  wire [25:2] MAR_q;
  wire [31:0] bit_extender_1_out, demultiplexer_2_out0, demultiplexer_2_out1, multiplexer_2_out;

  and and_1 (Unaligned, ~SIZE, or_1_out);  // AND_Gate
  and and_2 (SW, STORE, ~SIZE);  // AND_Gate
  not not_1 (L, STORE);
  or or_1 (or_1_out, BYTE[1], BYTE[0]);
  Register #(.width(32)) MAR (.D(MAR_IN), .en(LD_MAR), .Q({CRAP, MAR_q, BYTE}), .clk(CK));  // open: clr
  not not_2 (not_2_out, or_2_out);
  or or_2 (or_2_out, SW, demultiplexer_1_out0);
  not not_3 (not_3_out, or_3_out);
  or or_3 (or_3_out, SW, demultiplexer_1_out1);
  not not_4 (not_4_out, or_4_out);
  or or_4 (or_4_out, SW, demultiplexer_1_out2);
  not not_5 (not_5_out, or_5_out);
  or or_5 (or_5_out, SW, demultiplexer_1_out3);
  RAM #(.addrWidth(24)) ram_1 (.addr(MAR_q), .data(ram_1_data), .clk(CK), .ld(not_2_out));  // open: sel, clr
  assign ram_1_data = demultiplexer_1_out0 ? MDR_IN_t : 8'bz;  // Controlled_Buffer controlled_buffer_1
  RAM #(.addrWidth(24)) ram_2 (.addr(MAR_q), .data(ram_2_data), .clk(CK), .ld(not_3_out));  // open: sel, clr
  assign ram_2_data = demultiplexer_1_out1 ? MDR_IN_t : 8'bz;  // Controlled_Buffer controlled_buffer_2
  RAM #(.addrWidth(24)) ram_3 (.addr(MAR_q), .data(ram_3_data), .clk(CK), .ld(not_4_out));  // open: sel, clr
  RAM #(.addrWidth(24)) ram_4 (.addr(MAR_q), .data(ram_4_data), .clk(CK), .ld(not_5_out));  // open: sel, clr
  Demultiplexer #(.select(2), .disabled(0), .enable("false")) demultiplexer_1 (
    .out0(demultiplexer_1_out0), .out1(demultiplexer_1_out1), .out2(demultiplexer_1_out2),
    .out3(demultiplexer_1_out3), .in(not_6_out), .sel(BYTE));
  not not_6 (not_6_out, L);
  assign ram_3_data = demultiplexer_1_out2 ? MDR_IN_t : 8'bz;  // Controlled_Buffer controlled_buffer_3
  assign ram_4_data = demultiplexer_1_out3 ? MDR_IN_t : 8'bz;  // Controlled_Buffer controlled_buffer_4
  and and_3 (and_3_out, ~SIZE, ~L);  // AND_Gate
  Multiplexer #(.select(2), .width(8), .disabled(0), .enable("false")) multiplexer_1 (
    .in0(ram_1_data), .in1(ram_2_data), .in2(ram_3_data), .in3(ram_4_data), .out(multiplexer_1_out),
    .sel(BYTE));
  Demultiplexer #(.width(32), .disabled(0), .enable("false")) demultiplexer_2 (
    .out0(demultiplexer_2_out0), .out1(demultiplexer_2_out1), .in(MDR_IN), .sel(SIZE));
  assign {ram_4_data, ram_3_data, ram_2_data, ram_1_data} = and_3_out ? demultiplexer_2_out0 : 32'bz;  // Controlled_Buffer controlled_buffer_5
  assign bit_extender_1_out = {{24{1'b0}}, multiplexer_1_out};  // Bit_Extender bit_extender_1
  Bit_Extender #(.in_width(32), .out_width(8)) bit_extender_2 (.in(demultiplexer_2_out1), .out(MDR_IN_t));
  Multiplexer #(.width(32), .disabled(0), .enable("false")) multiplexer_2 (
    .in0({ram_4_data, ram_3_data, ram_2_data, ram_1_data}), .in1(bit_extender_1_out),
    .out(multiplexer_2_out), .sel(SIZE));
  Register #(.width(32)) MDR (.D(multiplexer_2_out), .en(LD_MDR), .Q(MDR_OUT), .clk(CK));  // open: clr
endmodule

module register_file (
  input  [3:0] DST_REG,
  input  [31:0] DATA_IN,
  input  [3:0] REG_A,
  input  [3:0] REG_B,
  input  CK,
  input  WE,
  output [31:0] OUT_A,
  output [31:0] OUT_B
);

  wire A_0, B_0, demultiplexer_1_out0, demultiplexer_1_out1, demultiplexer_1_out2, demultiplexer_1_out3,
       or_1_out, or_2_out;
  wire [31:0] multiplexer_2_out, multiplexer_4_out, register_group_1_out_a, register_group_1_out_b,
       register_group_2_out_a, register_group_2_out_b, register_group_3_out_a, register_group_3_out_b,
       register_group_4_out_a, register_group_4_out_b;

  not not_1 (A_0, or_1_out);
  or or_1 (or_1_out, REG_A[3], REG_A[2], REG_A[1], REG_A[0]);
  or or_2 (or_2_out, REG_B[3], REG_B[2], REG_B[1], REG_B[0]);
  not not_2 (B_0, or_2_out);
  Demultiplexer #(.select(2), .disabled(0), .enable("false")) demultiplexer_1 (
    .out0(demultiplexer_1_out0), .out1(demultiplexer_1_out1), .out2(demultiplexer_1_out2),
    .out3(demultiplexer_1_out3), .in(WE), .sel(DST_REG[3:2]));
  register_group register_group_1 (
    .REG_A(REG_A[1:0]), .REG_B(REG_B[1:0]), .DATA_IN(DATA_IN), .DST_REG(DST_REG[1:0]),
    .WE(demultiplexer_1_out0), .CK(CK), .OUT_A(register_group_1_out_a), .OUT_B(register_group_1_out_b));
  register_group register_group_2 (
    .REG_A(REG_A[1:0]), .REG_B(REG_B[1:0]), .DATA_IN(DATA_IN), .DST_REG(DST_REG[1:0]),
    .WE(demultiplexer_1_out1), .CK(CK), .OUT_A(register_group_2_out_a), .OUT_B(register_group_2_out_b));
  register_group register_group_3 (
    .REG_A(REG_A[1:0]), .REG_B(REG_B[1:0]), .DATA_IN(DATA_IN), .DST_REG(DST_REG[1:0]),
    .WE(demultiplexer_1_out2), .CK(CK), .OUT_A(register_group_3_out_a), .OUT_B(register_group_3_out_b));
  register_group register_group_4 (
    .REG_A(REG_A[1:0]), .REG_B(REG_B[1:0]), .DATA_IN(DATA_IN), .DST_REG(DST_REG[1:0]),
    .WE(demultiplexer_1_out3), .CK(CK), .OUT_A(register_group_4_out_a), .OUT_B(register_group_4_out_b));
  Multiplexer #(.width(32), .disabled(0), .enable("false")) multiplexer_1 (
    .in0(multiplexer_2_out), .in1({32{1'b0}}), .out(OUT_A), .sel(A_0));
  Multiplexer #(.select(2), .width(32), .disabled(0), .enable("false")) multiplexer_2 (
    .in0(register_group_1_out_a), .in1(register_group_2_out_a), .in2(register_group_3_out_a),
    .in3(register_group_4_out_a), .out(multiplexer_2_out), .sel(REG_A[3:2]));
  Multiplexer #(.width(32), .disabled(0), .enable("false")) multiplexer_3 (
    .in0(multiplexer_4_out), .in1({32{1'b0}}), .out(OUT_B), .sel(B_0));
  Multiplexer #(.select(2), .width(32), .disabled(0), .enable("false")) multiplexer_4 (
    .in0(register_group_1_out_b), .in1(register_group_2_out_b), .in2(register_group_3_out_b),
    .in3(register_group_4_out_b), .out(multiplexer_4_out), .sel(REG_B[3:2]));

  // Other names for the same wires on the sheet: D_REG[1:0] = DST_REG[1:0]; D_GRP[1:0] = DST_REG[3:2];
  //   A_REG[1:0] = REG_A[1:0]; A_GRP[1:0] = REG_A[3:2]; B_REG[1:0] = REG_B[1:0]; B_GRP[1:0] = REG_B[3:2]
endmodule

module register_group (
  input  [31:0] DATA_IN,
  input  [1:0] DST_REG,
  input  [1:0] REG_A,
  input  [1:0] REG_B,
  input  WE,
  input  CK,
  output [31:0] OUT_A,
  output [31:0] OUT_B
);

  wire demultiplexer_1_out0, demultiplexer_1_out1, demultiplexer_1_out2, demultiplexer_1_out3;
  wire [31:0] register_1_q, register_2_q, register_3_q, register_4_q;

  Demultiplexer #(.select(2), .disabled(0), .enable("false")) demultiplexer_1 (
    .out0(demultiplexer_1_out0), .out1(demultiplexer_1_out1), .out2(demultiplexer_1_out2),
    .out3(demultiplexer_1_out3), .in(WE), .sel(DST_REG));
  Register #(.width(32)) register_1 (.D(DATA_IN), .en(demultiplexer_1_out0), .Q(register_1_q), .clk(CK));  // open: clr
  Register #(.width(32)) register_2 (.D(DATA_IN), .en(demultiplexer_1_out1), .Q(register_2_q), .clk(CK));  // open: clr
  Register #(.width(32)) register_3 (.D(DATA_IN), .en(demultiplexer_1_out2), .Q(register_3_q), .clk(CK));  // open: clr
  Register #(.width(32)) register_4 (.D(DATA_IN), .en(demultiplexer_1_out3), .Q(register_4_q), .clk(CK));  // open: clr
  Multiplexer #(.select(2), .width(32), .disabled(0), .enable("false")) multiplexer_1 (
    .in0(register_1_q), .in1(register_2_q), .in2(register_3_q), .in3(register_4_q), .out(OUT_A), .sel(REG_A));
  Multiplexer #(.select(2), .width(32), .disabled(0), .enable("false")) multiplexer_2 (
    .in0(register_1_q), .in1(register_2_q), .in2(register_3_q), .in3(register_4_q), .out(OUT_B), .sel(REG_B));
endmodule

module ALU (
  input  [2:0] SELECT,
  input  [31:0] INPUT_A,
  input  [31:0] INPUT_B,
  output [31:0] OUTPUT
);

  wire [31:0] adder_1_out, and_1_out, not_1_out, not_2_out, shifter_1_out, subtractor_1_out;

  Adder #(.width(32)) adder_1 (.a(INPUT_A), .b(INPUT_B), .out(adder_1_out));  // open: cin, cout
  assign and_1_out = INPUT_A & INPUT_B;  // AND_Gate and_1, 32 bits wide
  assign not_1_out = ~INPUT_A;  // NOT_Gate not_1, 32 bits wide
  Shifter #(.width(32), .shift("ar")) shifter_1 (.in(INPUT_A), .\dist (INPUT_B[4:0]), .out(shifter_1_out));
  Subtractor #(.width(32)) subtractor_1 (.a(INPUT_A), .b(INPUT_B), .out(subtractor_1_out));  // open: bin, bout
  assign not_2_out = ~and_1_out;  // NOT_Gate not_2, 32 bits wide
  Multiplexer #(.select(3), .width(32), .disabled(0), .enable("false")) multiplexer_1 (
    .in0(adder_1_out), .in1(not_2_out), .in2(not_1_out), .in3(shifter_1_out), .in4(and_1_out),
    .in5(subtractor_1_out), .out(OUTPUT), .sel(SELECT));  // open: in6, in7

  // Other names for the same wires on the sheet: IN_A[31:0] = INPUT_A; IN_B[31:0] = INPUT_B
endmodule

module Immediate_Calc (
  input  [17:0] Immediate_Value,
  input  PCOFF,
  output [31:0] OUTPUT
);

  wire [31:0] bit_extender_1_out, multiplier_1_out;

  assign bit_extender_1_out = {{14{Immediate_Value[17]}}, Immediate_Value};  // Bit_Extender bit_extender_1
  Multiplier #(.width(32)) multiplier_1 (.a(bit_extender_1_out), .b(32'h4), .out(multiplier_1_out));  // open: cin, cout
  Multiplexer #(.width(32), .disabled(0), .enable("false")) multiplexer_1 (
    .in0(bit_extender_1_out), .in1(multiplier_1_out), .out(OUTPUT), .sel(PCOFF));
endmodule

// CU
module Control_Unit (
  input  Z,
  input  CK,
  input  [5:0] OPCODE,
  input  [1:0] Interrupt,
  output [19:0] DATA_PATH
);

  wire USE_DECODE, USE_Z;
  wire [4:0] CURR__STATE, DEC_NEXT, multiplexer_1_out, multiplexer_2_out, NEXT_STATE, Z_NEXT;

  Multiplexer #(.width(5), .disabled(0), .enable("false")) multiplexer_1 (
    .in0(NEXT_STATE), .in1(Z_NEXT), .out(multiplexer_1_out), .sel(USE_Z));
  Multiplexer #(.width(5), .disabled(0), .enable("false")) multiplexer_2 (
    .in0(multiplexer_1_out), .in1(DEC_NEXT), .out(multiplexer_2_out), .sel(USE_DECODE));
  ROM #(.addrWidth(5), .dataWidth(27)) rom_1 (
    .addr(CURR__STATE), .data({DATA_PATH, NEXT_STATE, USE_Z, USE_DECODE}));  // open: sel
  Register #(.width(5)) register_1 (.D(multiplexer_2_out), .en(1'b1), .Q(CURR__STATE), .clk(CK));  // open: clr
  ROM #(.addrWidth(2), .dataWidth(5)) rom_2 (.addr({1'b0, Z}), .data(Z_NEXT));  // open: sel
  ROM #(.addrWidth(6), .dataWidth(5)) rom_3 (.addr(OPCODE), .data(DEC_NEXT));  // open: sel

  // Notes on the sheet:
  //   contents of rom_1 (hex, n*v repeats v):
  //   4180004 40008 220064 810000 810080 2010018 500400 810100 811180 811000 811800 1081030 40034 210000
  //   108103c 42040 210000 1081048 404000 1081050 406000 811200 8086dc 2 901c00 1
  //   contents of rom_2 (hex, n*v repeats v):
  //   0 18
  //   contents of rom_3 (hex, n*v repeats v):
  //   3 4 7 13*0 9 8 15 0 b e 11 13 a 7*0 5 16
endmodule

module interrupt_control (
  input  [31:0] in_1,
  input  Unaligned,
  input  IntACK,
  input  Clock,
  output [31:0] BUS,
  output Int
);

  wire shift_register_1_p3;

  Register #(.width(1)) IntR (.D(Unaligned), .Q(Int), .clk(Unaligned), .clr(IntACK));  // open: en
  assign BUS = shift_register_1_p3 ? in_1 : 32'bz;  // Controlled_Buffer controlled_buffer_1
  // Shift_Register #(.length(2), .parallel("false")) shift_register_1: pin names not known; wires that end beside it: IntACK, Clock, shift_register_1_p3
endmodule
