// Logisim project LC-2200.circ as structural Verilog: 8 circuits, main circuit my circuit
module my_circuit (
);

  wire ADD_IMM, BYTE, CK, DrALU, DrALU2, DrMEM, DrPC, DrPC2, DrREG, IE, InkAck, Int, interrupt_control_1_int,
       JUMP, LD_IE, LD_IR, LD_MAR, LD_MDR, LD_PC, LD_RG, LD_Z, nor_1_out, not_1_out, or_1_out, or_2_out, RTI,
       SavePC, Unaligned, Z;
  wire [2:0] ALU;
  wire [3:0] multiplexer_2_out, multiplexer_3_out, multiplexer_4_out, multiplexer_5_out;
  wire [4:1] Misc;
  wire [5:0] OPCODE;
  wire [17:0] IMM;
  wire [25:18] IR_q;
  wire [31:0] adder_1_out, alu_1_output, bit_extender_1_out, Bus, controlled_buffer_1_out, memory_1_mdr_out,
       multiplexer_1_out, multiplexer_6_out, multiplexer_7_out, PC, register_file_1_out_a,
       register_file_1_out_b;

  Clock CLOCK (.out(CK));
  Adder #(.width(32)) adder_1 (.a(PC), .b(32'h4), .out(adder_1_out));  // open: cin, cout
  Multiplexer #(.width(32), .disabled(0), .enable("false")) multiplexer_1 (
    .in0(adder_1_out), .in1(Bus), .out(multiplexer_1_out), .sel(JUMP));
  Control_Unit control_unit_1 (
    .Z(Z), .OPCODE(OPCODE), .Interrupt(Int), .CK(CK),
    .DATA_PATH({DrPC, DrPC2, DrALU, DrALU2, DrREG, DrMEM, LD_PC, LD_MAR, LD_MDR, LD_IR, LD_RG, LD_Z, Misc[4], BYTE, ADD_IMM, Misc[1], JUMP, ALU, LD_IE, InkAck}));
  assign controlled_buffer_1_out = DrPC ? PC : 32'bz;  // Controlled_Buffer controlled_buffer_1
  Register #(.width(32)) u_PC (.D(multiplexer_1_out), .en(LD_PC), .Q(PC), .clk(CK));  // open: clr
  and and_1 (RTI, OPCODE[1], OPCODE[4], OPCODE[5]);
  assign Bus = DrPC2 ? PC : 32'bz;  // Controlled_Buffer controlled_buffer_2
  Register #(.width(32)) IR (.D(Bus), .en(LD_IR), .Q({OPCODE, IR_q, IMM}), .clk(CK));  // open: clr
  Multiplexer #(.width(4), .disabled(0), .enable("false")) multiplexer_2 (
    .in0(IR_q[25:22]), .in1(IR_q[21:18]), .out(multiplexer_2_out), .sel(JUMP));
  or or_1 (or_1_out, Misc[4], JUMP);
  Multiplexer #(.width(4), .disabled(0), .enable("false")) multiplexer_3 (
    .in0(IMM[3:0]), .in1(IR_q[25:22]), .out(multiplexer_3_out), .sel(or_1_out));
  Multiplexer #(.width(4), .disabled(0), .enable("false")) multiplexer_4 (
    .in0(multiplexer_2_out), .in1(4'b1100), .out(multiplexer_4_out), .sel(SavePC));
  register_file register_file_1 (
    .REG_A(IR_q[21:18]), .REG_B(multiplexer_5_out), .DST_REG(multiplexer_4_out), .DATA_IN(Bus), .WE(LD_RG),
    .CK(CK), .OUT_A(register_file_1_out_a), .OUT_B(register_file_1_out_b));
  Multiplexer #(.width(4), .disabled(0), .enable("false")) multiplexer_5 (
    .in0(multiplexer_3_out), .in1(4'b1100), .out(multiplexer_5_out), .sel(SavePC));
  nor nor_1 (nor_1_out, Bus[31], Bus[30], Bus[29], Bus[28], Bus[27], Bus[26], Bus[25], Bus[24], Bus[23], Bus[22], Bus[21], Bus[20], Bus[19], Bus[18], Bus[17], Bus[16], Bus[15], Bus[14], Bus[13], Bus[12], Bus[11], Bus[10], Bus[9], Bus[8], Bus[7], Bus[6], Bus[5], Bus[4], Bus[3], Bus[2], Bus[1], Bus[0]);
  Register #(.width(1)) u_Z (.D(nor_1_out), .en(LD_Z), .Q(Z), .clk(CK));  // open: clr
  assign Bus = DrREG ? register_file_1_out_b : 32'bz;  // Controlled_Buffer controlled_buffer_3
  interrupt_control interrupt_control_1 (
    .Unaligned(Unaligned), .IntACK(InkAck), .Clock(CK), .BUS(Bus), .Int(interrupt_control_1_int));
  and and_2 (SavePC, ALU[0], ALU[1], ALU[2]);
  Multiplexer #(.width(32), .disabled(0), .enable("false")) multiplexer_6 (
    .in0(register_file_1_out_a), .in1(PC), .out(multiplexer_6_out), .sel(Misc[1]));
  Multiplexer #(.width(32), .disabled(0), .enable("false")) multiplexer_7 (
    .in0(register_file_1_out_b), .in1(bit_extender_1_out), .out(multiplexer_7_out), .sel(ADD_IMM));
  assign bit_extender_1_out = {{14{IMM[17]}}, IMM};  // Bit_Extender bit_extender_1
  and and_3 (Int, interrupt_control_1_int, IE);
  assign controlled_buffer_1_out = DrALU ? alu_1_output : 32'bz;  // Controlled_Buffer controlled_buffer_4
  ALU alu_1 (.INPUT_A(multiplexer_6_out), .INPUT_B(multiplexer_7_out), .SELECT(ALU), .OUTPUT(alu_1_output));
  assign Bus = DrALU2 ? alu_1_output : 32'bz;  // Controlled_Buffer controlled_buffer_5
  not not_1 (not_1_out, SavePC);
  or or_2 (or_2_out, not_1_out, RTI);
  memory memory_1 (
    .MAR_IN(controlled_buffer_1_out), .Unaligned(Unaligned), .MDR_IN(Bus), .CK(CK), .STORE(Misc[4]),
    .SIZE(BYTE), .LD_MAR(LD_MAR), .LD_MDR(LD_MDR), .MDR_OUT(memory_1_mdr_out));
  assign Bus = DrMEM ? memory_1_mdr_out : 32'bz;  // Controlled_Buffer controlled_buffer_6
  Register #(.width(1)) u_IE (.D(or_2_out), .en(LD_IE), .Q(IE), .clk(CK));  // open: clr

  // Other names for the same wires on the sheet: Misc (some bits) = {BYTE, ADD_IMM, JUMP}; PCOFF = Misc[1];
  //   STORE = Misc[4]; LOAD[5:0] = {LD_PC, LD_MAR, LD_MDR, LD_IR, LD_RG, LD_Z};
  //   DRs[5:0] = {DrPC, DrPC2, DrALU, DrALU2, DrREG, DrMEM}

  // Notes on the sheet:
  //   CLOCK
  //   Eric Peyton
  //   GTID: 902705905
endmodule

module memory (
  input  [31:0] MDR_IN,
  input  [31:0] MAR_IN,
  input  LD_MAR,
  input  LD_MDR,
  input  CK,
  input  STORE,
  input  SIZE,
  output Unaligned,
  output [31:0] MDR_OUT
);

  wire and_3_out, and_4_out, and_5_out, and_6_out, and_7_out, demultiplexer_1_out0, demultiplexer_1_out1,
       demultiplexer_1_out2, demultiplexer_1_out3, L, not_2_out, not_3_out, not_4_out, not_5_out, not_6_out,
       or_1_out, or_2_out, or_3_out, or_4_out, or_5_out, SW;
  wire [1:0] BYTE;
  wire [5:0] CRAP;
  wire [7:0] MDR_IN_t, multiplexer_1_out, ram_1_data, ram_2_data, ram_3_data, ram_4_data;
  wire [25:2] MAR_q;
  wire [31:0] bit_extender_1_out, demultiplexer_2_out0, demultiplexer_2_out1, multiplexer_2_out;

  and and_1 (Unaligned, ~SIZE, or_1_out);  // AND_Gate
  and and_2 (SW, STORE, ~SIZE);  // AND_Gate
  not not_1 (L, STORE);
  or or_1 (or_1_out, BYTE[1], BYTE[0]);
  Register #(.width(32)) MAR (.D(MAR_IN), .en(LD_MAR), .Q({CRAP, MAR_q, BYTE}), .clk(CK));  // open: clr
  not not_2 (not_2_out, or_2_out);
  or or_2 (or_2_out, SW, demultiplexer_1_out0);
  not not_3 (not_3_out, or_3_out);
  or or_3 (or_3_out, SW, demultiplexer_1_out1);
  not not_4 (not_4_out, or_4_out);
  or or_4 (or_4_out, SW, demultiplexer_1_out2);
  not not_5 (not_5_out, or_5_out);
  or or_5 (or_5_out, SW, demultiplexer_1_out3);
  RAM #(.addrWidth(24)) ram_1 (.addr(MAR_q), .data(ram_1_data), .clk(CK), .ld(not_2_out));  // open: sel, clr
  RAM #(.addrWidth(24)) ram_2 (.addr(MAR_q), .data(ram_2_data), .clk(CK), .ld(not_3_out));  // open: sel, clr
  RAM #(.addrWidth(24)) ram_3 (.addr(MAR_q), .data(ram_3_data), .clk(CK), .ld(not_4_out));  // open: sel, clr
  RAM #(.addrWidth(24)) ram_4 (.addr(MAR_q), .data(ram_4_data), .clk(CK), .ld(not_5_out));  // open: sel, clr
  Demultiplexer #(.select(2), .disabled(0), .enable("false")) demultiplexer_1 (
    .out0(demultiplexer_1_out0), .out1(demultiplexer_1_out1), .out2(demultiplexer_1_out2),
    .out3(demultiplexer_1_out3), .in(not_6_out), .sel(BYTE));
  not not_6 (not_6_out, L);
  assign ram_1_data = and_3_out ? MDR_IN_t : 8'bz;  // Controlled_Buffer controlled_buffer_1
  and and_3 (and_3_out, SIZE, demultiplexer_1_out0);
  assign ram_2_data = and_4_out ? MDR_IN_t : 8'bz;  // Controlled_Buffer controlled_buffer_2
  and and_4 (and_4_out, SIZE, demultiplexer_1_out1);
  assign ram_3_data = and_5_out ? MDR_IN_t : 8'bz;  // Controlled_Buffer controlled_buffer_3
  and and_5 (and_5_out, SIZE, demultiplexer_1_out2);
  assign ram_4_data = and_6_out ? MDR_IN_t : 8'bz;  // Controlled_Buffer controlled_buffer_4
  and and_6 (and_6_out, SIZE, demultiplexer_1_out3);
  and and_7 (and_7_out, ~SIZE, ~L);  // AND_Gate
  Multiplexer #(.select(2), .width(8), .disabled(0), .enable("false")) multiplexer_1 (
    .in0(ram_1_data), .in1(ram_2_data), .in2(ram_3_data), .in3(ram_4_data), .out(multiplexer_1_out),
    .sel(BYTE));
  Demultiplexer #(.width(32), .disabled(0), .enable("false")) demultiplexer_2 (
    .out0(demultiplexer_2_out0), .out1(demultiplexer_2_out1), .in(MDR_IN), .sel(SIZE));
  assign {ram_4_data, ram_3_data, ram_2_data, ram_1_data} = and_7_out ? demultiplexer_2_out0 : 32'bz;  // Controlled_Buffer controlled_buffer_5
  assign bit_extender_1_out = {{24{1'b0}}, multiplexer_1_out};  // Bit_Extender bit_extender_1
  Bit_Extender #(.in_width(32), .out_width(8)) bit_extender_2 (.in(demultiplexer_2_out1), .out(MDR_IN_t));
  Multiplexer #(.width(32), .disabled(0), .enable("false")) multiplexer_2 (
    .in0({ram_4_data, ram_3_data, ram_2_data, ram_1_data}), .in1(bit_extender_1_out),
    .out(multiplexer_2_out), .sel(SIZE));
  Register #(.width(32)) MDR (.D(multiplexer_2_out), .en(LD_MDR), .Q(MDR_OUT), .clk(CK));  // open: clr
endmodule

module register_file (
  input  [3:0] DST_REG,
  input  [31:0] DATA_IN,
  input  [3:0] REG_A,
  input  [3:0] REG_B,
  input  CK,
  input  WE,
  output [31:0] OUT_A,
  output [31:0] OUT_B
);

  wire A_0, B_0, demultiplexer_1_out0, demultiplexer_1_out1, demultiplexer_1_out2, demultiplexer_1_out3,
       or_1_out, or_2_out;
  wire [31:0] multiplexer_2_out, multiplexer_4_out, register_group_1_out_a, register_group_1_out_b,
       register_group_2_out_a, register_group_2_out_b, register_group_3_out_a, register_group_3_out_b,
       register_group_4_out_a, register_group_4_out_b;

  not not_1 (A_0, or_1_out);
  or or_1 (or_1_out, REG_A[3], REG_A[2], REG_A[1], REG_A[0]);
  or or_2 (or_2_out, REG_B[3], REG_B[2], REG_B[1], REG_B[0]);
  not not_2 (B_0, or_2_out);
  Demultiplexer #(.select(2), .disabled(0), .enable("false")) demultiplexer_1 (
    .out0(demultiplexer_1_out0), .out1(demultiplexer_1_out1), .out2(demultiplexer_1_out2),
    .out3(demultiplexer_1_out3), .in(WE), .sel(DST_REG[3:2]));
  register_group register_group_1 (
    .REG_A(REG_A[1:0]), .REG_B(REG_B[1:0]), .DATA_IN(DATA_IN), .DST_REG(DST_REG[1:0]),
    .WE(demultiplexer_1_out0), .CK(CK), .OUT_A(register_group_1_out_a), .OUT_B(register_group_1_out_b));
  register_group register_group_2 (
    .REG_A(REG_A[1:0]), .REG_B(REG_B[1:0]), .DATA_IN(DATA_IN), .DST_REG(DST_REG[1:0]),
    .WE(demultiplexer_1_out1), .CK(CK), .OUT_A(register_group_2_out_a), .OUT_B(register_group_2_out_b));
  register_group register_group_3 (
    .REG_A(REG_A[1:0]), .REG_B(REG_B[1:0]), .DATA_IN(DATA_IN), .DST_REG(DST_REG[1:0]),
    .WE(demultiplexer_1_out2), .CK(CK), .OUT_A(register_group_3_out_a), .OUT_B(register_group_3_out_b));
  register_group register_group_4 (
    .REG_A(REG_A[1:0]), .REG_B(REG_B[1:0]), .DATA_IN(DATA_IN), .DST_REG(DST_REG[1:0]),
    .WE(demultiplexer_1_out3), .CK(CK), .OUT_A(register_group_4_out_a), .OUT_B(register_group_4_out_b));
  Multiplexer #(.width(32), .disabled(0), .enable("false")) multiplexer_1 (
    .in0(multiplexer_2_out), .in1({32{1'b0}}), .out(OUT_A), .sel(A_0));
  Multiplexer #(.select(2), .width(32), .disabled(0), .enable("false")) multiplexer_2 (
    .in0(register_group_1_out_a), .in1(register_group_2_out_a), .in2(register_group_3_out_a),
    .in3(register_group_4_out_a), .out(multiplexer_2_out), .sel(REG_A[3:2]));
  Multiplexer #(.width(32), .disabled(0), .enable("false")) multiplexer_3 (
    .in0(multiplexer_4_out), .in1({32{1'b0}}), .out(OUT_B), .sel(B_0));
  Multiplexer #(.select(2), .width(32), .disabled(0), .enable("false")) multiplexer_4 (
    .in0(register_group_1_out_b), .in1(register_group_2_out_b), .in2(register_group_3_out_b),
    .in3(register_group_4_out_b), .out(multiplexer_4_out), .sel(REG_B[3:2]));

  // Other names for the same wires on the sheet: D_REG[1:0] = DST_REG[1:0]; D_GRP[1:0] = DST_REG[3:2];
  //   A_REG[1:0] = REG_A[1:0]; A_GRP[1:0] = REG_A[3:2]; B_REG[1:0] = REG_B[1:0]; B_GRP[1:0] = REG_B[3:2]
endmodule

module register_group (
  input  [31:0] DATA_IN,
  input  [1:0] DST_REG,
  input  [1:0] REG_A,
  input  [1:0] REG_B,
  input  WE,
  input  CK,
  output [31:0] OUT_A,
  output [31:0] OUT_B
);

  wire demultiplexer_1_out0, demultiplexer_1_out1, demultiplexer_1_out2, demultiplexer_1_out3;
  wire [31:0] register_1_q, register_2_q, register_3_q, register_4_q;

  Demultiplexer #(.select(2), .disabled(0), .enable("false")) demultiplexer_1 (
    .out0(demultiplexer_1_out0), .out1(demultiplexer_1_out1), .out2(demultiplexer_1_out2),
    .out3(demultiplexer_1_out3), .in(WE), .sel(DST_REG));
  Register #(.width(32)) register_1 (.D(DATA_IN), .en(demultiplexer_1_out0), .Q(register_1_q), .clk(CK));  // open: clr
  Register #(.width(32)) register_2 (.D(DATA_IN), .en(demultiplexer_1_out1), .Q(register_2_q), .clk(CK));  // open: clr
  Register #(.width(32)) register_3 (.D(DATA_IN), .en(demultiplexer_1_out2), .Q(register_3_q), .clk(CK));  // open: clr
  Register #(.width(32)) register_4 (.D(DATA_IN), .en(demultiplexer_1_out3), .Q(register_4_q), .clk(CK));  // open: clr
  Multiplexer #(.select(2), .width(32), .disabled(0), .enable("false")) multiplexer_1 (
    .in0(register_1_q), .in1(register_2_q), .in2(register_3_q), .in3(register_4_q), .out(OUT_A), .sel(REG_A));
  Multiplexer #(.select(2), .width(32), .disabled(0), .enable("false")) multiplexer_2 (
    .in0(register_1_q), .in1(register_2_q), .in2(register_3_q), .in3(register_4_q), .out(OUT_B), .sel(REG_B));
endmodule

module ALU (
  input  [2:0] SELECT,
  input  [31:0] INPUT_A,
  input  [31:0] INPUT_B,
  output [31:0] OUTPUT
);

  wire [31:0] adder_1_out, and_1_out, not_1_out, not_2_out, shifter_1_out, subtractor_1_out;

  Adder #(.width(32)) adder_1 (.a(INPUT_A), .b(INPUT_B), .out(adder_1_out));  // open: cin, cout
  assign and_1_out = INPUT_A & INPUT_B;  // AND_Gate and_1, 32 bits wide
  assign not_1_out = ~INPUT_A;  // NOT_Gate not_1, 32 bits wide
  Shifter #(.width(32), .shift("ar")) shifter_1 (.in(INPUT_A), .\dist (INPUT_B[4:0]), .out(shifter_1_out));
  Subtractor #(.width(32)) subtractor_1 (.a(INPUT_A), .b(INPUT_B), .out(subtractor_1_out));  // open: bin, bout
  assign not_2_out = ~and_1_out;  // NOT_Gate not_2, 32 bits wide
  Multiplexer #(.select(3), .width(32), .disabled(0), .enable("false")) multiplexer_1 (
    .in0(adder_1_out), .in1(not_2_out), .in2(not_1_out), .in3(shifter_1_out), .in4(and_1_out),
    .in5(subtractor_1_out), .out(OUTPUT), .sel(SELECT));  // open: in6, in7

  // Other names for the same wires on the sheet: IN_A[31:0] = INPUT_A; IN_B[31:0] = INPUT_B
endmodule

module Immediate_Calc (
  input  [17:0] Immediate_Value,
  input  PCOFF,
  output [31:0] OUTPUT
);

  wire [31:0] bit_extender_1_out, multiplier_1_out;

  assign bit_extender_1_out = {{14{Immediate_Value[17]}}, Immediate_Value};  // Bit_Extender bit_extender_1
  Multiplier #(.width(32)) multiplier_1 (.a(bit_extender_1_out), .b(32'h4), .out(multiplier_1_out));  // open: cin, cout
  Multiplexer #(.width(32), .disabled(0), .enable("false")) multiplexer_1 (
    .in0(bit_extender_1_out), .in1(multiplier_1_out), .out(OUTPUT), .sel(PCOFF));
endmodule

// CU
module Control_Unit (
  input  Z,
  input  CK,
  input  [5:0] OPCODE,
  input  Interrupt,
  output [21:0] DATA_PATH
);

  wire USE_DECODE, USE_Z;
  wire [4:0] CURR__STATE, DEC_NEXT, INT_NEXT, multiplexer_1_out, NEXT_STATE, Z_NEXT;

  Multiplexer #(.select(2), .width(5), .disabled(0), .enable("false")) multiplexer_1 (
    .in0(NEXT_STATE), .in1(DEC_NEXT), .in2(Z_NEXT), .in3(INT_NEXT), .out(multiplexer_1_out),
    .sel({USE_Z, USE_DECODE}));
  ROM #(.addrWidth(5), .dataWidth(29)) rom_1 (
    .addr(CURR__STATE), .data({DATA_PATH, NEXT_STATE, USE_Z, USE_DECODE}));  // open: sel
  Register #(.width(5)) register_1 (.D(multiplexer_1_out), .en(1'b1), .Q(CURR__STATE), .clk(CK));  // open: clr
  ROM #(.addrWidth(2), .dataWidth(5)) rom_2 (.addr({1'b0, Z}), .data(Z_NEXT));  // open: sel
  ROM #(.addrWidth(6), .dataWidth(5)) rom_3 (.addr(OPCODE), .data(DEC_NEXT));  // open: sel
  ROM #(.addrWidth(2), .dataWidth(5)) rom_4 (.addr({1'b0, Interrupt}), .data(INT_NEXT));  // open: sel

  // Notes on the sheet:
  //   contents of rom_1 (hex, n*v repeats v):
  //   3 100008 880064 2040000 2040200 8041018 1401000 2040400 2044600 2044000 2046000 4204030 100034
  //   840000 420403c 108040 840000 4204048 1010000 4204050 1018000 2044800 2021a5c 2 2407000 1 8040fec
  //   401000 f00 100 1401f00 10600004
  //   contents of rom_2 (hex, n*v repeats v):
  //   0 18
  //   contents of rom_3 (hex, n*v repeats v):
  //   3 4 7 13*0 9 8 15 0 b e 11 13 a 7*0 5 16 14*0 1c 1d 1e
  //   contents of rom_4 (hex, n*v repeats v):
  //   1f 1a
endmodule

module interrupt_control (
  input  Unaligned,
  input  IntACK,
  input  Clock,
  output [31:0] BUS,
  output Int
);

  wire shift_register_1_out;

  Register #(.width(1)) Interrupt (.D(Unaligned), .Q(Int), .clk(Unaligned), .clr(IntACK));  // open: en
  assign BUS = shift_register_1_out ? 32'h30 : 32'bz;  // Controlled_Buffer controlled_buffer_1
  Shift_Register #(.length(1), .parallel("false")) shift_register_1 (
    .in(IntACK), .clk(Clock), .out(shift_register_1_out));  // open: shift, load, clr, d0, q0
endmodule
