// Logisim project PipelinedLC2200.circ as structural Verilog: 13 circuits, main circuit my circuit
module my_circuit (
);

  wire CK, CLOCK_out, HALT, JALR, LD_REG, not_1_out, PC_FB, register_file_1_stall, Z;
  wire [1:0] D_FB, E_FB, F_FB;
  wire [3:0] dbuf_1_reg_dst_out, ebuf_1_reg_dst_out, fbuf_1_reg_dst_out, fbuf_1_reg_sr1_out,
       fbuf_1_reg_sr2_out, REG_DST;
  wire [7:0] dbuf_1_opcode_out, ebuf_1_opcode_out, fbuf_1_opcode_out, mbuf_1_opcode_out;
  wire [15:0] fbuf_1_immediate_val_out;
  wire [31:0] alu_1_out, BEQ_PC, bit_extender_1_out, counter_1_q, d_mem_1_data_out, dbuf_1_imm_out,
       dbuf_1_pc_out, dbuf_1_sr1_out, dbuf_1_sr2_out, DST_VAL, ebuf_1_alu_val_out, ebuf_1_word_val_out,
       fbuf_1_pc_out, i_mem_1_data_out, JALR_PC, multiplexer_1_out, PC, PC_q, register_file_1_out_b;

  Adder #(.width(32)) adder_1 (.a(PC_q), .b(32'h1), .out(PC));  // open: cin, cout
  Multiplexer #(.select(2), .width(32), .disabled(0), .enable("false")) multiplexer_1 (
    .in0(PC), .in1(BEQ_PC), .in2(JALR_PC), .in3(BEQ_PC), .out(multiplexer_1_out), .sel({JALR, Z}));
  Register #(.width(32)) u_PC (.D(multiplexer_1_out), .en(not_1_out), .Q(PC_q), .clk(CK));  // open: clr
  not not_1 (not_1_out, PC_FB);
  I_MEM i_mem_1 (.ADDRESS(PC_q), .DATA_OUT(i_mem_1_data_out), .CLOCK(CK));
  and and_1 (CK, CLOCK_out, ~HALT);  // AND_Gate
  Clock CLOCK (.out(CLOCK_out));
  // Probe on REG_DST
  FBUF fbuf_1 (
    .PC_IN(PC), .INPUT(i_mem_1_data_out), .FEEBACK_OUT(PC_FB), .FEEDBACK_IN(F_FB), .CLOCK(CK),
    .PC_OUT(fbuf_1_pc_out), .OPCODE_OUT(fbuf_1_opcode_out), .REG_DST_OUT(fbuf_1_reg_dst_out),
    .REG_SR1_OUT(fbuf_1_reg_sr1_out), .REG_SR2_OUT(fbuf_1_reg_sr2_out),
    .IMMEDIATE_VAL_OUT(fbuf_1_immediate_val_out));
  Counter #(.width(32), .max('hffffffff), .ongoal("stay")) counter_1 (
    .count(CK), .Q(counter_1_q), .clk(CK));  // open: load, D, carry, clr
  Register_File register_file_1 (
    .REG_A(fbuf_1_reg_sr1_out), .REG_B(fbuf_1_reg_sr2_out), .OUT_A(JALR_PC), .OUT_B(register_file_1_out_b),
    .DST_REG(REG_DST), .DATA_IN(DST_VAL), .WE(LD_REG), .CK(CK), .ALT_B(fbuf_1_reg_dst_out),
    .OPCODE_IN(fbuf_1_opcode_out), .JALR(JALR), .STALL(register_file_1_stall), .FLUSH(F_FB));
  assign bit_extender_1_out = {{16{fbuf_1_immediate_val_out[15]}}, fbuf_1_immediate_val_out};  // Bit_Extender bit_extender_1
  // Probe on counter_1_q
  // Probe on DST_VAL
  DBUF dbuf_1 (
    .PC_IN(fbuf_1_pc_out), .OPCODE_IN(fbuf_1_opcode_out), .REG_DST_IN(fbuf_1_reg_dst_out), .SR1_IN(JALR_PC),
    .SR2_IN(register_file_1_out_b), .IMM_IN(bit_extender_1_out), .JALR_IN(JALR),
    .STALL(register_file_1_stall), .PC_OUT(dbuf_1_pc_out), .OPCODE_OUT(dbuf_1_opcode_out),
    .REG_DST_OUT(dbuf_1_reg_dst_out), .SR1_OUT(dbuf_1_sr1_out), .SR2_OUT(dbuf_1_sr2_out),
    .IMM_OUT(dbuf_1_imm_out), .FEEBACK_OUT(F_FB), .FEEDBACK_IN(D_FB), .CLOCK(CK));
  ALU alu_1 (
    .A_IN(dbuf_1_sr1_out), .B_IN(dbuf_1_sr2_out), .OUT(alu_1_out), .OPCODE(dbuf_1_opcode_out),
    .IMM_IN(dbuf_1_imm_out), .PC_IN(dbuf_1_pc_out), .ALT_OUT(BEQ_PC), .ZERO(Z));
  EBUF ebuf_1 (
    .PC_IN(dbuf_1_pc_out), .OPCODE_IN(dbuf_1_opcode_out), .REG_DST_IN(dbuf_1_reg_dst_out),
    .ALU_VAL_IN(alu_1_out), .WORD_VAL_IN(BEQ_PC), .Z_IN(Z), .FEEBACK_OUT(D_FB), .FEEDBACK_IN(E_FB),
    .CLOCK(CK), .OPCODE_OUT(ebuf_1_opcode_out), .REG_DST_OUT(ebuf_1_reg_dst_out),
    .ALU_VAL_OUT(ebuf_1_alu_val_out), .WORD_VAL_OUT(ebuf_1_word_val_out));  // open: PC_OUT
  D_MEM d_mem_1 (
    .ADDRESS(ebuf_1_alu_val_out), .DATA_OUT(d_mem_1_data_out), .DATA_IN(ebuf_1_word_val_out),
    .OPCODE(ebuf_1_opcode_out), .CLOCK(CK));
  Opcode_Dissector opcode_dissector_1 (
    .OPCODE_IN(mbuf_1_opcode_out), .LD_REG(LD_REG));  // open: USE_PC, USE_IMMEDIATE, ALU_SEL, MEM_OP, EXTRA, STORE_WORD, BEQ, JALR
  MBUF mbuf_1 (
    .OPCODE_IN(ebuf_1_opcode_out), .REG_DST_IN(ebuf_1_reg_dst_out), .MEM_VAL_IN(d_mem_1_data_out),
    .FEEBACK_OUT(E_FB), .CLOCK(CK), .HALT(HALT), .OPCODE_OUT(mbuf_1_opcode_out), .REG_DST_OUT(REG_DST),
    .MEM_VAL_OUT(DST_VAL));
endmodule

// F\nBUF
module FBUF (
  input  [1:0] FEEDBACK_IN,
  input  [31:0] PC_IN,
  input  [31:0] INPUT,
  input  CLOCK,
  output [31:0] PC_OUT,
  output FEEBACK_OUT,
  output [7:0] OPCODE_OUT,
  output [3:0] REG_DST_OUT,
  output [3:0] REG_SR1_OUT,
  output [3:0] REG_SR2_OUT,
  output [15:0] IMMEDIATE_VAL_OUT
);

  wire not_1_out, or_1_out;
  wire [31:0] multiplexer_1_out;

  Multiplexer #(.width(32), .disabled(0), .enable("false")) multiplexer_1 (
    .in0(INPUT), .in1({32{1'b0}}), .out(multiplexer_1_out), .sel(FEEDBACK_IN[1]));
  or or_1 (or_1_out, FEEDBACK_IN[1], not_1_out);
  not not_1 (not_1_out, FEEDBACK_IN[0]);
  Register #(.width(32)) PC (.D(PC_IN), .en(or_1_out), .Q(PC_OUT), .clk(CLOCK));  // open: clr
  Register #(.width(32)) FBUF (
    .D(multiplexer_1_out), .en(or_1_out), .Q({OPCODE_OUT, REG_DST_OUT, REG_SR1_OUT, IMMEDIATE_VAL_OUT}),
    .clk(CLOCK));  // open: clr

  assign FEEBACK_OUT = FEEDBACK_IN[0];
  assign REG_SR2_OUT = IMMEDIATE_VAL_OUT[15:12];

  // Other names for the same wires on the sheet: OP[7:0] = OPCODE_OUT; STIN = FEEDBACK_IN[0]; FLSH = FEEDBACK_IN[1]
endmodule

// D\nBUF
module DBUF (
  input  [1:0] FEEDBACK_IN,
  input  [31:0] PC_IN,
  input  [7:0] OPCODE_IN,
  input  [3:0] REG_DST_IN,
  input  [31:0] SR1_IN,
  input  [31:0] SR2_IN,
  input  [31:0] IMM_IN,
  input  CLOCK,
  input  JALR_IN,
  input  STALL,
  output [1:0] FEEBACK_OUT,
  output [31:0] PC_OUT,
  output [7:0] OPCODE_OUT,
  output [3:0] REG_DST_OUT,
  output [31:0] SR1_OUT,
  output [31:0] SR2_OUT,
  output [31:0] IMM_OUT
);

  wire JALR, LD, not_1_out, or_1_out;
  wire [7:0] multiplexer_1_out;

  Multiplexer #(.width(8), .disabled(0), .enable("false")) multiplexer_1 (
    .in0(OPCODE_IN), .in1({8{1'b0}}), .out(multiplexer_1_out), .sel(or_1_out));
  or or_1 (or_1_out, FEEDBACK_IN[1], STALL);
  and and_1 (JALR, JALR_IN, ~STALL);  // AND_Gate
  Register #(.width(32)) PC (.D(PC_IN), .en(LD), .Q(PC_OUT), .clk(CLOCK));  // open: clr
  Register OPCODE (.D(multiplexer_1_out), .en(LD), .Q(OPCODE_OUT), .clk(CLOCK));  // open: clr
  Register #(.width(4)) REG_DST (.D(REG_DST_IN), .en(LD), .Q(REG_DST_OUT), .clk(CLOCK));  // open: clr
  Register #(.width(32)) SR1_VAL (.D(SR1_IN), .en(LD), .Q(SR1_OUT), .clk(CLOCK));  // open: clr
  Register #(.width(32)) SR2_VAL (.D(SR2_IN), .en(LD), .Q(SR2_OUT), .clk(CLOCK));  // open: clr
  Register #(.width(32)) IMM_VAL (.D(IMM_IN), .en(LD), .Q(IMM_OUT), .clk(CLOCK));  // open: clr
  assign FEEBACK_OUT = {JALR, STALL} | FEEDBACK_IN;  // OR_Gate or_2, 2 bits wide
  or or_3 (LD, not_1_out, FEEDBACK_IN[1]);
  not not_1 (not_1_out, FEEDBACK_IN[0]);

  // Other names for the same wires on the sheet: STOT = STALL; CK = CLOCK; STIN = FEEDBACK_IN[0];
  //   FLSH = FEEDBACK_IN[1]
endmodule

// E\nBUF
module EBUF (
  input  [1:0] FEEDBACK_IN,
  input  [31:0] PC_IN,
  input  [7:0] OPCODE_IN,
  input  [3:0] REG_DST_IN,
  input  [31:0] ALU_VAL_IN,
  input  [31:0] WORD_VAL_IN,
  input  Z_IN,
  input  CLOCK,
  output [1:0] FEEBACK_OUT,
  output [31:0] PC_OUT,
  output [7:0] OPCODE_OUT,
  output [3:0] REG_DST_OUT,
  output [31:0] ALU_VAL_OUT,
  output [31:0] WORD_VAL_OUT
);

  wire LD, not_1_out;
  wire [7:0] multiplexer_1_out;

  Multiplexer #(.width(8), .disabled(0), .enable("false")) multiplexer_1 (
    .in0(OPCODE_IN), .in1({8{1'b0}}), .out(multiplexer_1_out), .sel(FEEDBACK_IN[1]));
  Register #(.width(32)) PC (.D(PC_IN), .en(LD), .Q(PC_OUT), .clk(CLOCK));  // open: clr
  Register OPCODE (.D(multiplexer_1_out), .en(LD), .Q(OPCODE_OUT), .clk(CLOCK));  // open: clr
  Register #(.width(4)) REG_DST (.D(REG_DST_IN), .en(LD), .Q(REG_DST_OUT), .clk(CLOCK));  // open: clr
  Register #(.width(32)) ALU_VAL (.D(ALU_VAL_IN), .en(LD), .Q(ALU_VAL_OUT), .clk(CLOCK));  // open: clr
  Register #(.width(32)) WORD_VAL (.D(WORD_VAL_IN), .en(LD), .Q(WORD_VAL_OUT), .clk(CLOCK));  // open: clr
  not not_1 (not_1_out, FEEDBACK_IN[0]);
  assign FEEBACK_OUT = {Z_IN, 1'b0} | FEEDBACK_IN;  // OR_Gate or_1, 2 bits wide
  or or_2 (LD, not_1_out, FEEDBACK_IN[1]);

  // Other names for the same wires on the sheet: Z = Z_IN; CK = CLOCK; STLL = FEEDBACK_IN[0]; FLSH = FEEDBACK_IN[1]
endmodule

// M\nBUF
module MBUF (
  input  [7:0] OPCODE_IN,
  input  [3:0] REG_DST_IN,
  input  [31:0] MEM_VAL_IN,
  input  CLOCK,
  output [1:0] FEEBACK_OUT,
  output [7:0] OPCODE_OUT,
  output [3:0] REG_DST_OUT,
  output [31:0] MEM_VAL_OUT,
  output HALT
);

  Register OPCODE (.D(OPCODE_IN), .en(1'b1), .Q(OPCODE_OUT), .clk(CLOCK));  // open: clr
  Register #(.width(4)) REG_DST (.D(REG_DST_IN), .en(1'b1), .Q(REG_DST_OUT), .clk(CLOCK));  // open: clr
  Register #(.width(32)) MEM_VAL (.D(MEM_VAL_IN), .en(1'b1), .Q(MEM_VAL_OUT), .clk(CLOCK));  // open: clr
  Comparator #(.mode("unsigned")) comparator_1 (.a(OPCODE_OUT), .b({8{1'b1}}), .eq(HALT));  // open: gt, lt

  assign FEEBACK_OUT = 2'b00;

  // Other names for the same wires on the sheet: CK = CLOCK; OP[7:0] = OPCODE_OUT
endmodule

module ALU (
  input  [7:0] OPCODE,
  input  [31:0] PC_IN,
  input  [31:0] A_IN,
  input  [31:0] B_IN,
  input  [31:0] IMM_IN,
  output [31:0] OUT,
  output [31:0] ALT_OUT,
  output ZERO
);

  wire BEQ, comparator_1_eq, USE_IMM, USE_PC;
  wire [1:0] opcode_dissector_1_alu_sel;
  wire [31:0] A, adder_1_out, adder_2_out, and_1_out, B, not_1_out, subtractor_1_out;

  Multiplexer #(.width(32), .disabled(0), .enable("false")) multiplexer_1 (
    .in0(A_IN), .in1(PC_IN), .out(A), .sel(USE_PC));
  Multiplexer #(.width(32), .disabled(0), .enable("false")) multiplexer_2 (
    .in0(B_IN), .in1(IMM_IN), .out(B), .sel(USE_IMM));
  Opcode_Dissector opcode_dissector_1 (
    .USE_PC(USE_PC), .USE_IMMEDIATE(USE_IMM), .ALU_SEL(opcode_dissector_1_alu_sel), .OPCODE_IN(OPCODE),
    .BEQ(BEQ));  // open: MEM_OP, LD_REG, EXTRA, STORE_WORD, JALR
  Adder #(.width(32)) adder_1 (.a(A), .b(B), .out(adder_1_out));  // open: cin, cout
  assign not_1_out = ~and_1_out;  // NOT_Gate not_1, 32 bits wide
  assign and_1_out = A & B;  // AND_Gate and_1, 32 bits wide
  Subtractor #(.width(32)) subtractor_1 (.a(A), .b(B), .out(subtractor_1_out));  // open: bin, bout
  Multiplexer #(.select(2), .width(32), .disabled(0), .enable("false")) multiplexer_3 (
    .in0(adder_1_out), .in1(not_1_out), .in2(subtractor_1_out), .in3(A), .out(OUT),
    .sel(opcode_dissector_1_alu_sel));
  Comparator #(.width(32), .mode("unsigned")) comparator_1 (
    .a({32{1'b0}}), .b(OUT), .eq(comparator_1_eq));  // open: gt, lt
  Adder #(.width(32)) adder_2 (.a(PC_IN), .b(IMM_IN), .out(adder_2_out));  // open: cin, cout
  and and_2 (ZERO, comparator_1_eq, BEQ);
  Multiplexer #(.width(32), .disabled(0), .enable("false")) multiplexer_4 (
    .in0(B_IN), .in1(adder_2_out), .out(ALT_OUT), .sel(ZERO));

  // Other names for the same wires on the sheet: IMM[31:0] = IMM_IN; PC[31:0] = PC_IN; Z = ZERO
endmodule

// REG \nFILE
module Register_File (
  input  [7:0] OPCODE_IN,
  input  [3:0] DST_REG,
  input  [31:0] DATA_IN,
  input  [3:0] REG_A,
  input  [3:0] REG_B,
  input  [3:0] ALT_B,
  input  [1:0] FLUSH,
  input  CK,
  input  WE,
  output [31:0] OUT_A,
  output [31:0] OUT_B,
  output JALR,
  output STALL
);

  wire A_0, and_1_out, B_0, b_register_file_1_a_out, b_register_file_1_b_out, demultiplexer_1_out0,
       demultiplexer_1_out1, demultiplexer_1_out2, demultiplexer_1_out3, LD_REG, opcode_dissector_1_beq,
       opcode_dissector_1_store_word, USE_ALT;
  wire [3:0] B;
  wire [31:0] multiplexer_2_out, multiplexer_4_out, register_group_1_out_a, register_group_1_out_b,
       register_group_2_out_a, register_group_2_out_b, register_group_3_out_a, register_group_3_out_b,
       register_group_4_out_a, register_group_4_out_b;

  Multiplexer #(.width(4), .disabled(0), .enable("false")) multiplexer_1 (
    .in0(REG_B), .in1(ALT_B), .out(B), .sel(USE_ALT));
  Opcode_Dissector opcode_dissector_1 (
    .OPCODE_IN(OPCODE_IN), .LD_REG(LD_REG), .STORE_WORD(opcode_dissector_1_store_word),
    .BEQ(opcode_dissector_1_beq), .JALR(JALR));  // open: USE_PC, USE_IMMEDIATE, ALU_SEL, MEM_OP, EXTRA
  Comparator #(.width(4), .mode("unsigned")) comparator_1 (.a(4'b0000), .b(REG_A), .eq(A_0));  // open: gt, lt
  Comparator #(.width(4), .mode("unsigned")) comparator_2 (.a(B), .b(4'b0000), .eq(B_0));  // open: gt, lt
  or or_1 (USE_ALT, opcode_dissector_1_store_word, opcode_dissector_1_beq);
  B_Register_File b_register_file_1 (
    .REG_A(REG_A), .REG_B(B), .BUSY_REG(ALT_B), .CLR_REG(DST_REG), .BUSY_IN(and_1_out), .BUSY_WE(LD_REG),
    .CLOCK(CK), .CLEAR(WE), .A_OUT(b_register_file_1_a_out), .B_OUT(b_register_file_1_b_out));
  and and_1 (and_1_out, ~FLUSH[1], LD_REG);  // AND_Gate
  or or_2 (STALL, b_register_file_1_a_out, b_register_file_1_b_out);
  Demultiplexer #(.select(2), .disabled(0), .enable("false")) demultiplexer_1 (
    .out0(demultiplexer_1_out0), .out1(demultiplexer_1_out1), .out2(demultiplexer_1_out2),
    .out3(demultiplexer_1_out3), .in(WE), .sel(DST_REG[3:2]));
  Register_Group register_group_1 (
    .REG_A(REG_A[1:0]), .REG_B(B[1:0]), .DATA_IN(DATA_IN), .DST_REG(DST_REG[1:0]), .WE(demultiplexer_1_out0),
    .CK(CK), .OUT_A(register_group_1_out_a), .OUT_B(register_group_1_out_b));
  Register_Group register_group_2 (
    .REG_A(REG_A[1:0]), .REG_B(B[1:0]), .DATA_IN(DATA_IN), .DST_REG(DST_REG[1:0]), .WE(demultiplexer_1_out1),
    .CK(CK), .OUT_A(register_group_2_out_a), .OUT_B(register_group_2_out_b));
  Register_Group register_group_3 (
    .REG_A(REG_A[1:0]), .REG_B(B[1:0]), .DATA_IN(DATA_IN), .DST_REG(DST_REG[1:0]), .WE(demultiplexer_1_out2),
    .CK(CK), .OUT_A(register_group_3_out_a), .OUT_B(register_group_3_out_b));
  Register_Group register_group_4 (
    .REG_A(REG_A[1:0]), .REG_B(B[1:0]), .DATA_IN(DATA_IN), .DST_REG(DST_REG[1:0]), .WE(demultiplexer_1_out3),
    .CK(CK), .OUT_A(register_group_4_out_a), .OUT_B(register_group_4_out_b));
  Multiplexer #(.select(2), .width(32), .disabled(0), .enable("false")) multiplexer_2 (
    .in0(register_group_1_out_a), .in1(register_group_2_out_a), .in2(register_group_3_out_a),
    .in3(register_group_4_out_a), .out(multiplexer_2_out), .sel(REG_A[3:2]));
  Multiplexer #(.width(32), .disabled(0), .enable("false")) multiplexer_3 (
    .in0(multiplexer_2_out), .in1({32{1'b0}}), .out(OUT_A), .sel(A_0));
  Multiplexer #(.select(2), .width(32), .disabled(0), .enable("false")) multiplexer_4 (
    .in0(register_group_1_out_b), .in1(register_group_2_out_b), .in2(register_group_3_out_b),
    .in3(register_group_4_out_b), .out(multiplexer_4_out), .sel(B[3:2]));
  Multiplexer #(.width(32), .disabled(0), .enable("false")) multiplexer_5 (
    .in0(multiplexer_4_out), .in1({32{1'b0}}), .out(OUT_B), .sel(B_0));

  // Other names for the same wires on the sheet: A[3:0] = REG_A; A_REG[1:0] = REG_A[1:0]; A_GRP[1:0] = REG_A[3:2];
  //   B_REG[1:0] = B[1:0]; B_GRP[1:0] = B[3:2]; D_REG[1:0] = DST_REG[1:0]; DST[3:0] = DST_REG;
  //   D_GRP[1:0] = DST_REG[3:2]; FUT_DST[3:0] = ALT_B
endmodule

module Register_Group (
  input  [31:0] DATA_IN,
  input  [1:0] DST_REG,
  input  [1:0] REG_A,
  input  [1:0] REG_B,
  input  CK,
  input  WE,
  output [31:0] OUT_A,
  output [31:0] OUT_B
);

  wire demultiplexer_1_out0, demultiplexer_1_out1, demultiplexer_1_out2, demultiplexer_1_out3;
  wire [31:0] register_1_q, register_2_q, register_3_q, register_4_q;

  Demultiplexer #(.select(2), .disabled(0), .enable("false")) demultiplexer_1 (
    .out0(demultiplexer_1_out0), .out1(demultiplexer_1_out1), .out2(demultiplexer_1_out2),
    .out3(demultiplexer_1_out3), .in(WE), .sel(DST_REG));
  Register #(.width(32)) register_1 (.D(DATA_IN), .en(demultiplexer_1_out0), .Q(register_1_q), .clk(CK));  // open: clr
  Register #(.width(32)) register_2 (.D(DATA_IN), .en(demultiplexer_1_out1), .Q(register_2_q), .clk(CK));  // open: clr
  Register #(.width(32)) register_3 (.D(DATA_IN), .en(demultiplexer_1_out2), .Q(register_3_q), .clk(CK));  // open: clr
  Register #(.width(32)) register_4 (.D(DATA_IN), .en(demultiplexer_1_out3), .Q(register_4_q), .clk(CK));  // open: clr
  Multiplexer #(.select(2), .width(32), .disabled(0), .enable("false")) multiplexer_1 (
    .in0(register_1_q), .in1(register_2_q), .in2(register_3_q), .in3(register_4_q), .out(OUT_A), .sel(REG_A));
  Multiplexer #(.select(2), .width(32), .disabled(0), .enable("false")) multiplexer_2 (
    .in0(register_1_q), .in1(register_2_q), .in2(register_3_q), .in3(register_4_q), .out(OUT_B), .sel(REG_B));
endmodule

// I\nMEM
module I_MEM (
  input  [31:0] ADDRESS,
  input  CLOCK,
  output [31:0] DATA_OUT
);

  wire not_1_out;

  not not_1 (not_1_out, 1'b0);
  RAM #(.addrWidth(24), .dataWidth(32), .bus("separate")) ram_1 (
    .addr(ADDRESS[23:0]), .din({32{1'b0}}), .data(DATA_OUT), .str(1'b0), .clk(CLOCK), .ld(not_1_out));  // open: sel, clr

  // Other names for the same wires on the sheet: TRASH[7:0] = ADDRESS[31:24]
endmodule

// DISSECT
module Opcode_Dissector (
  input  [7:0] OPCODE_IN,
  output BEQ,
  output JALR,
  output STORE_WORD,
  output USE_PC,
  output USE_IMMEDIATE,
  output [1:0] ALU_SEL,
  output [1:0] MEM_OP,
  output LD_REG,
  output EXTRA
);

  Decoder #(.select(2), .enable("false")) decoder_1 (
    .out2(STORE_WORD), .sel(OPCODE_IN[3:2]));  // open: out0, out1, out3
  Decoder #(.select(2), .enable("false")) decoder_2 (
    .out1(BEQ), .out3(JALR), .sel(OPCODE_IN[1:0]));  // open: out0, out2

  assign ALU_SEL = OPCODE_IN[5:4];
  assign EXTRA = OPCODE_IN[0];
  assign LD_REG = OPCODE_IN[1];
  assign MEM_OP = OPCODE_IN[3:2];
  assign USE_IMMEDIATE = OPCODE_IN[6];
  assign USE_PC = OPCODE_IN[7];

  // Other names for the same wires on the sheet: EXTRA_t[1:0] = OPCODE_IN[1:0]
endmodule

// D\nMEM
module D_MEM (
  input  [7:0] OPCODE,
  input  [31:0] DATA_IN,
  input  [31:0] ADDRESS,
  input  CLOCK,
  output [31:0] DATA_OUT
);

  wire STORE;
  wire [1:0] opcode_dissector_1_mem_op;
  wire [31:0] ram_1_data;

  RAM #(.addrWidth(24), .dataWidth(32), .bus("separate")) ram_1 (
    .addr(ADDRESS[23:0]), .din(DATA_IN), .data(ram_1_data), .str(STORE), .clk(CLOCK));  // open: sel, ld, clr
  Opcode_Dissector opcode_dissector_1 (
    .MEM_OP(opcode_dissector_1_mem_op), .OPCODE_IN(OPCODE), .STORE_WORD(STORE));  // open: USE_PC, USE_IMMEDIATE, ALU_SEL, LD_REG, EXTRA, BEQ, JALR
  Multiplexer #(.select(2), .width(32), .disabled(0), .enable("false")) multiplexer_1 (
    .in0(ADDRESS), .in1(ram_1_data), .out(DATA_OUT), .sel(opcode_dissector_1_mem_op));  // open: in2, in3

  // Other names for the same wires on the sheet: PASS[31:0] = ADDRESS; TRASH[7:0] = ADDRESS[31:24]
endmodule

// BUSY
module B_Register_File (
  input  BUSY_IN,
  input  [3:0] REG_A,
  input  [3:0] REG_B,
  input  [3:0] CLR_REG,
  input  [3:0] BUSY_REG,
  input  CLOCK,
  input  BUSY_WE,
  input  CLEAR,
  output A_OUT,
  output B_OUT
);

  wire CRP_0, CRP_1, CRP_2, CRP_3, demultiplexer_1_out0, demultiplexer_1_out1, demultiplexer_1_out2,
       demultiplexer_1_out3, demultiplexer_2_out0, demultiplexer_2_out1, demultiplexer_2_out2,
       demultiplexer_2_out3, demultiplexer_3_out0, demultiplexer_3_out1, demultiplexer_3_out2,
       demultiplexer_3_out3, demultiplexer_4_out0, demultiplexer_4_out1, demultiplexer_4_out2,
       demultiplexer_4_out3, demultiplexer_6_out0, demultiplexer_6_out1, demultiplexer_6_out2,
       demultiplexer_6_out3, demultiplexer_7_out0, demultiplexer_7_out1, demultiplexer_7_out2,
       demultiplexer_7_out3, demultiplexer_8_out0, demultiplexer_8_out1, demultiplexer_8_out2,
       demultiplexer_8_out3, demultiplexer_9_out0, demultiplexer_9_out1, demultiplexer_9_out2,
       demultiplexer_9_out3, GRP_0, GRP_1, GRP_2, GRP_3, shift_register_2_out;
  wire [1:0] CRG;
  wire [3:0] _0_OUT, _1_OUT, _2_OUT, _3_OUT;
  wire [3:2] shift_register_1_out;
  wire [15:0] decoder_1_out0, decoder_2_out0;

  Demultiplexer #(.select(2), .disabled(0), .enable("false")) demultiplexer_1 (
    .out0(demultiplexer_1_out0), .out1(demultiplexer_1_out1), .out2(demultiplexer_1_out2),
    .out3(demultiplexer_1_out3), .in(GRP_0), .sel(BUSY_REG[1:0]));
  Demultiplexer #(.select(2), .disabled(0), .enable("false")) demultiplexer_2 (
    .out0(demultiplexer_2_out0), .out1(demultiplexer_2_out1), .out2(demultiplexer_2_out2),
    .out3(demultiplexer_2_out3), .in(CRP_0), .sel(CRG));
  Demultiplexer #(.select(2), .disabled(0), .enable("false")) demultiplexer_3 (
    .out0(demultiplexer_3_out0), .out1(demultiplexer_3_out1), .out2(demultiplexer_3_out2),
    .out3(demultiplexer_3_out3), .in(GRP_1), .sel(BUSY_REG[1:0]));
  Demultiplexer #(.select(2), .disabled(0), .enable("false")) demultiplexer_4 (
    .out0(demultiplexer_4_out0), .out1(demultiplexer_4_out1), .out2(demultiplexer_4_out2),
    .out3(demultiplexer_4_out3), .in(CRP_1), .sel(CRG));
  Demultiplexer #(.select(2), .disabled(0), .enable("false")) demultiplexer_5 (
    .out0(GRP_0), .out1(GRP_1), .out2(GRP_2), .out3(GRP_3), .in(BUSY_WE), .sel(BUSY_REG[3:2]));
  Register #(.width(1)) register_1 (
    .D(BUSY_IN), .en(demultiplexer_1_out0), .Q(_0_OUT[0]), .clk(CLOCK), .clr(demultiplexer_2_out0));
  Register #(.width(1)) register_2 (
    .D(BUSY_IN), .en(demultiplexer_1_out1), .Q(_0_OUT[1]), .clk(CLOCK), .clr(demultiplexer_2_out1));
  Register #(.width(1)) register_3 (
    .D(BUSY_IN), .en(demultiplexer_1_out2), .Q(_0_OUT[2]), .clk(CLOCK), .clr(demultiplexer_2_out2));
  Register #(.width(1)) register_4 (
    .D(BUSY_IN), .en(demultiplexer_1_out3), .Q(_0_OUT[3]), .clk(CLOCK), .clr(demultiplexer_2_out3));
  Register #(.width(1)) register_5 (
    .D(BUSY_IN), .en(demultiplexer_3_out0), .Q(_1_OUT[0]), .clk(CLOCK), .clr(demultiplexer_4_out0));
  Register #(.width(1)) register_6 (
    .D(BUSY_IN), .en(demultiplexer_3_out1), .Q(_1_OUT[1]), .clk(CLOCK), .clr(demultiplexer_4_out1));
  Register #(.width(1)) register_7 (
    .D(BUSY_IN), .en(demultiplexer_3_out2), .Q(_1_OUT[2]), .clk(CLOCK), .clr(demultiplexer_4_out2));
  Register #(.width(1)) register_8 (
    .D(BUSY_IN), .en(demultiplexer_3_out3), .Q(_1_OUT[3]), .clk(CLOCK), .clr(demultiplexer_4_out3));
  Demultiplexer #(.select(2), .disabled(0), .enable("false")) demultiplexer_6 (
    .out0(demultiplexer_6_out0), .out1(demultiplexer_6_out1), .out2(demultiplexer_6_out2),
    .out3(demultiplexer_6_out3), .in(GRP_2), .sel(BUSY_REG[1:0]));
  Demultiplexer #(.select(2), .disabled(0), .enable("false")) demultiplexer_7 (
    .out0(demultiplexer_7_out0), .out1(demultiplexer_7_out1), .out2(demultiplexer_7_out2),
    .out3(demultiplexer_7_out3), .in(CRP_2), .sel(CRG));
  Demultiplexer #(.select(2), .disabled(0), .enable("false")) demultiplexer_8 (
    .out0(demultiplexer_8_out0), .out1(demultiplexer_8_out1), .out2(demultiplexer_8_out2),
    .out3(demultiplexer_8_out3), .in(GRP_3), .sel(BUSY_REG[1:0]));
  Demultiplexer #(.select(2), .disabled(0), .enable("false")) demultiplexer_9 (
    .out0(demultiplexer_9_out0), .out1(demultiplexer_9_out1), .out2(demultiplexer_9_out2),
    .out3(demultiplexer_9_out3), .in(CRP_3), .sel(CRG));
  Shift_Register #(.width(4), .length(1), .parallel("false")) shift_register_1 (
    .in(CLR_REG), .clk(CLOCK), .out({shift_register_1_out, CRG}));  // open: shift, load, clr, d0, q0
  Register #(.width(1)) register_9 (
    .D(BUSY_IN), .en(demultiplexer_6_out0), .Q(_2_OUT[0]), .clk(CLOCK), .clr(demultiplexer_7_out0));
  Register #(.width(1)) register_10 (
    .D(BUSY_IN), .en(demultiplexer_6_out1), .Q(_2_OUT[1]), .clk(CLOCK), .clr(demultiplexer_7_out1));
  Register #(.width(1)) register_11 (
    .D(BUSY_IN), .en(demultiplexer_6_out2), .Q(_2_OUT[2]), .clk(CLOCK), .clr(demultiplexer_7_out2));
  Register #(.width(1)) register_12 (
    .D(BUSY_IN), .en(demultiplexer_6_out3), .Q(_2_OUT[3]), .clk(CLOCK), .clr(demultiplexer_7_out3));
  Register #(.width(1)) register_13 (
    .D(BUSY_IN), .en(demultiplexer_8_out0), .Q(_3_OUT[0]), .clk(CLOCK), .clr(demultiplexer_9_out0));
  Register #(.width(1)) register_14 (
    .D(BUSY_IN), .en(demultiplexer_8_out1), .Q(_3_OUT[1]), .clk(CLOCK), .clr(demultiplexer_9_out1));
  Register #(.width(1)) register_15 (
    .D(BUSY_IN), .en(demultiplexer_8_out2), .Q(_3_OUT[2]), .clk(CLOCK), .clr(demultiplexer_9_out2));
  Register #(.width(1)) register_16 (
    .D(BUSY_IN), .en(demultiplexer_8_out3), .Q(_3_OUT[3]), .clk(CLOCK), .clr(demultiplexer_9_out3));
  Demultiplexer #(.select(2), .disabled(0), .enable("false")) demultiplexer_10 (
    .out0(CRP_0), .out1(CRP_1), .out2(CRP_2), .out3(CRP_3), .in(shift_register_2_out),
    .sel(shift_register_1_out));
  Shift_Register #(.length(1), .parallel("false")) shift_register_2 (
    .in(CLEAR), .clk(CLOCK), .out(shift_register_2_out));  // open: shift, load, clr, d0, q0
  Multiplexer #(.select(4), .disabled(0), .enable("false")) multiplexer_1 (
    .in0(_0_OUT[0]), .in1(_0_OUT[1]), .in2(_0_OUT[2]), .in3(_0_OUT[3]), .in4(_1_OUT[0]), .in5(_1_OUT[1]),
    .in6(_1_OUT[2]), .in7(_1_OUT[3]), .in8(_2_OUT[0]), .in9(_2_OUT[1]), .in10(_2_OUT[2]), .in11(_2_OUT[3]),
    .in12(_3_OUT[0]), .in13(_3_OUT[1]), .in14(_3_OUT[2]), .in15(_3_OUT[3]), .out(A_OUT), .sel(REG_A));
  Multiplexer #(.select(4), .disabled(0), .enable("false")) multiplexer_2 (
    .in0(_0_OUT[0]), .in1(_0_OUT[1]), .in2(_0_OUT[2]), .in3(_0_OUT[3]), .in4(_1_OUT[0]), .in5(_1_OUT[1]),
    .in6(_1_OUT[2]), .in7(_1_OUT[3]), .in8(_2_OUT[0]), .in9(_2_OUT[1]), .in10(_2_OUT[2]), .in11(_2_OUT[3]),
    .in12(_3_OUT[0]), .in13(_3_OUT[1]), .in14(_3_OUT[2]), .in15(_3_OUT[3]), .out(B_OUT), .sel(REG_B));
  Decoder #(.select(4), .enable("false")) decoder_1 (
    .out0(decoder_1_out0[0]), .out1(decoder_1_out0[1]), .out2(decoder_1_out0[2]), .out3(decoder_1_out0[3]),
    .out4(decoder_1_out0[4]), .out5(decoder_1_out0[5]), .out6(decoder_1_out0[6]), .out7(decoder_1_out0[7]),
    .out8(decoder_1_out0[8]), .out9(decoder_1_out0[9]), .out10(decoder_1_out0[10]),
    .out11(decoder_1_out0[11]), .out12(decoder_1_out0[12]), .out13(decoder_1_out0[13]),
    .out14(decoder_1_out0[14]), .out15(decoder_1_out0[15]));  // open: sel
  Decoder #(.select(4), .enable("false")) decoder_2 (
    .out0(decoder_2_out0[0]), .out1(decoder_2_out0[1]), .out2(decoder_2_out0[2]), .out3(decoder_2_out0[3]),
    .out4(decoder_2_out0[4]), .out5(decoder_2_out0[5]), .out6(decoder_2_out0[6]), .out7(decoder_2_out0[7]),
    .out8(decoder_2_out0[8]), .out9(decoder_2_out0[9]), .out10(decoder_2_out0[10]),
    .out11(decoder_2_out0[11]), .out12(decoder_2_out0[12]), .out13(decoder_2_out0[13]),
    .out14(decoder_2_out0[14]), .out15(decoder_2_out0[15]));  // open: sel
  // OR_Gate or_1 has open pins: in0=decoder_1_out0, in1=decoder_2_out0, out=open

  // Other names for the same wires on the sheet: RG[1:0] = BUSY_REG[1:0]; CK = CLOCK; IN = BUSY_IN
endmodule

module Data_Forward (
  input  [3:0] REG_IN,
  input  LD_RG,
  input  [31:0] DATA_IN,
  input  LD_DATA,
  input  CLOCK,
  output [3:0] REG_OUT,
  output [31:0] DATA_OUT,
  output VALID
);

  Register #(.width(4)) B_RP (.D(REG_IN), .en(LD_RG), .Q(REG_OUT), .clk(CLOCK));  // open: clr

  assign DATA_OUT = DATA_IN;
  assign VALID = LD_DATA;

  // Other names for the same wires on the sheet: CK = CLOCK; LDD = LD_DATA
endmodule
